// Logisim project cpu.circ as structural Verilog: 11 circuits, main circuit main
module main (
  input  clk,
  input  reset
);

  wire ALUSrc, Branch, Jump, MemtoReg, MemWrite, RegDst, RegWrite, Zero;
  wire [2:0] ALUControl;
  wire [4:0] multiplexer_1_out, spt_1__11_15, spt_1__16_20, spt_1__21_25;
  wire [15:0] spt_1__0_15;
  wire [31:0] alu_1_aluresult, dm_1_rd, grf_1_rd1, grf_1_rd2, Instr, multiplexer_2_out, multiplexer_3_out,
       PC, PC_prime, SignImm;

  PC pc_1 (.PC(PC_prime), .PC_prime(PC), .clk(clk));
  CU CU (
    .in(PC), .RegWrite(RegWrite), .MemWrite(MemWrite), .ALUControl(ALUControl), .RegDst(RegDst),
    .MemtoReg(MemtoReg), .ALUSrc(ALUSrc), .Branch(Branch), .Jump(Jump));
  IM im_1 (.PC(PC), .Instr(Instr));
  NXTAD nxtad_1 (
    .PC_prime(PC_prime), .PC(PC), .Zero(Zero), .Branch(Branch), .Jump(Jump), .Instr(Instr), .SignImm(SignImm));
  SPT spt_1 (.in(Instr), ._0_15(spt_1__0_15), ._16_20(spt_1__16_20), ._21_25(spt_1__21_25), ._11_15(spt_1__11_15));
  GRF grf_1 (
    .RD2(grf_1_rd2), .WD3(multiplexer_3_out), .RD1(grf_1_rd1), .WE3(RegWrite), .rst(reset), .clk(clk),
    .A1(spt_1__21_25), .A3(multiplexer_1_out), .A2(spt_1__16_20));
  EXT ext_1 (._15_0(spt_1__0_15), .SignImm(SignImm));
  Multiplexer #(.width(5), .enable("false")) multiplexer_1 (
    .in0(spt_1__16_20), .in1(spt_1__11_15), .out(multiplexer_1_out), .sel(RegDst));
  Multiplexer #(.width(32), .enable("false")) multiplexer_2 (
    .in0(grf_1_rd2), .in1(SignImm), .out(multiplexer_2_out), .sel(ALUSrc));
  ALU alu_1 (
    .SrcA(grf_1_rd1), .SrcB(multiplexer_2_out), .ALUResult(alu_1_aluresult), .ALUControl(ALUControl),
    .Zero(Zero));
  DM dm_1 (.A(alu_1_aluresult), .WD(grf_1_rd2), .RD(dm_1_rd), .clk(clk), .WE(MemWrite));
  Multiplexer #(.width(32), .enable("false")) multiplexer_3 (
    .in0(alu_1_aluresult), .in1(dm_1_rd), .out(multiplexer_3_out), .sel(MemtoReg));

  // Other names for the same wires on the sheet: rst = reset

  // Notes on the sheet:
  //   SignImm
  //   SrcB
  //   WriteData
  //   Result
endmodule

module PC (
  input  [31:0] PC,
  input  clk,
  output [31:0] PC_prime
);

  Register #(.width(32)) register_1 (.D(PC), .Q(PC_prime), .clk(clk));  // open: en, clr
endmodule

module IM (
  input  [31:0] PC,
  output [31:0] Instr
);

  ROM #(.addrWidth(5), .dataWidth(32)) rom_1 (.addr(PC[6:2]), .data(Instr));  // open: sel
endmodule

module DM (
  input  [31:0] A,
  input  [31:0] WD,
  input  clk,
  input  WE,
  output [31:0] RD
);

  RAM #(.addrWidth(5), .dataWidth(32), .bus("separate")) ram_1 (
    .addr(A[6:2]), .din(WD), .data(RD), .clk(clk), .ld(WE));  // open: str, sel, clr
endmodule

module GRF (
  input  [31:0] WD3,
  input  [4:0] A2,
  input  [4:0] A3,
  input  WE3,
  input  rst,
  input  clk,
  input  [4:0] A1,
  output [31:0] RD2,
  output [31:0] RD1
);

  wire [31:0] i0, i1, i2, i3, i4, i5, i6, i7, i8, i9, i10, i11, i12, i13, i14, i15, i16, i17, i18, i19, i20,
       i21, i22, i23, i24, i25, i26, i27, i28, i29, i30, i31, o0, o1, o2, o3, o4, o5, o6, o7, o8, o9, o10,
       o11, o12, o13, o14, o15, o16, o17, o18, o19, o20, o21, o22, o23, o24, o25, o26, o27, o28, o29, o30,
       o31;

  Register #(.width(32)) register_1 (.D(i0), .en(WE3), .Q(o0), .clk(clk), .clr(rst));
  Register #(.width(32)) register_2 (.D(i4), .en(WE3), .Q(o4), .clk(clk), .clr(rst));
  Register #(.width(32)) register_3 (.D(i8), .en(WE3), .Q(o8), .clk(clk), .clr(rst));
  Register #(.width(32)) register_4 (.D(i12), .en(WE3), .Q(o12), .clk(clk), .clr(rst));
  Register #(.width(32)) register_5 (.D(i16), .en(WE3), .Q(o16), .clk(clk), .clr(rst));
  Register #(.width(32)) register_6 (.D(i20), .en(WE3), .Q(o20), .clk(clk), .clr(rst));
  Register #(.width(32)) register_7 (.D(i24), .en(WE3), .Q(o24), .clk(clk), .clr(rst));
  Register #(.width(32)) register_8 (.D(i28), .en(WE3), .Q(o28), .clk(clk), .clr(rst));
  Register #(.width(32)) register_9 (.D(i1), .en(WE3), .Q(o1), .clk(clk), .clr(rst));
  Register #(.width(32)) register_10 (.D(i5), .en(WE3), .Q(o5), .clk(clk), .clr(rst));
  Register #(.width(32)) register_11 (.D(i9), .en(WE3), .Q(o9), .clk(clk), .clr(rst));
  Register #(.width(32)) register_12 (.D(i13), .en(WE3), .Q(o13), .clk(clk), .clr(rst));
  Register #(.width(32)) register_13 (.D(i17), .en(WE3), .Q(o17), .clk(clk), .clr(rst));
  Register #(.width(32)) register_14 (.D(i21), .en(WE3), .Q(o21), .clk(clk), .clr(rst));
  Register #(.width(32)) register_15 (.D(i25), .en(WE3), .Q(o25), .clk(clk), .clr(rst));
  Register #(.width(32)) register_16 (.D(i29), .en(WE3), .Q(o29), .clk(clk), .clr(rst));
  Register #(.width(32)) register_17 (.D(i2), .en(WE3), .Q(o2), .clk(clk), .clr(rst));
  Register #(.width(32)) register_18 (.D(i6), .en(WE3), .Q(o6), .clk(clk), .clr(rst));
  Register #(.width(32)) register_19 (.D(i10), .en(WE3), .Q(o10), .clk(clk), .clr(rst));
  Register #(.width(32)) register_20 (.D(i14), .en(WE3), .Q(o14), .clk(clk), .clr(rst));
  Register #(.width(32)) register_21 (.D(i18), .en(WE3), .Q(o18), .clk(clk), .clr(rst));
  Register #(.width(32)) register_22 (.D(i22), .en(WE3), .Q(o22), .clk(clk), .clr(rst));
  Register #(.width(32)) register_23 (.D(i26), .en(WE3), .Q(o26), .clk(clk), .clr(rst));
  Register #(.width(32)) register_24 (.D(i30), .en(WE3), .Q(o30), .clk(clk), .clr(rst));
  Register #(.width(32)) register_25 (.D(i3), .en(WE3), .Q(o3), .clk(clk), .clr(rst));
  Register #(.width(32)) register_26 (.D(i7), .en(WE3), .Q(o7), .clk(clk), .clr(rst));
  Register #(.width(32)) register_27 (.D(i11), .en(WE3), .Q(o11), .clk(clk), .clr(rst));
  Register #(.width(32)) register_28 (.D(i15), .en(WE3), .Q(o15), .clk(clk), .clr(rst));
  Register #(.width(32)) register_29 (.D(i19), .en(WE3), .Q(o19), .clk(clk), .clr(rst));
  Register #(.width(32)) register_30 (.D(i23), .en(WE3), .Q(o23), .clk(clk), .clr(rst));
  Register #(.width(32)) register_31 (.D(i27), .en(WE3), .Q(o27), .clk(clk), .clr(rst));
  Register #(.width(32)) register_32 (.D(i31), .en(WE3), .Q(o31), .clk(clk), .clr(rst));
  Multiplexer #(.select(5), .width(32), .enable("false")) multiplexer_1 (
    .in0(o0), .in1(o1), .in2(o2), .in3(o3), .in4(o4), .in5(o5), .in6(o6), .in7(o7), .in8(o8), .in9(o9),
    .in10(o10), .in11(o11), .in12(o12), .in13(o13), .in14(o14), .in15(o15), .in16(o16), .in17(o17),
    .in18(o18), .in19(o19), .in20(o20), .in21(o21), .in22(o22), .in23(o23), .in24(o24), .in25(o25),
    .in26(o26), .in27(o27), .in28(o28), .in29(o29), .in30(o30), .in31(o31), .out(RD1), .sel(A1));
  Demultiplexer #(.select(5), .width(32), .enable("false")) demultiplexer_1 (
    .out0(i0), .out1(i1), .out2(i2), .out3(i3), .out4(i4), .out5(i5), .out6(i6), .out7(i7), .out8(i8),
    .out9(i9), .out10(i10), .out11(i11), .out12(i12), .out13(i13), .out14(i14), .out15(i15), .out16(i16),
    .out17(i17), .out18(i18), .out19(i19), .out20(i20), .out21(i21), .out22(i22), .out23(i23), .out24(i24),
    .out25(i25), .out26(i26), .out27(i27), .out28(i28), .out29(i29), .out30(i30), .out31(i31), .in(WD3),
    .sel(A3));
  Multiplexer #(.select(5), .width(32), .enable("false")) multiplexer_2 (
    .in0(o0), .in1(o1), .in2(o2), .in3(o3), .in4(o4), .in5(o5), .in6(o6), .in7(o7), .in8(o8), .in9(o9),
    .in10(o10), .in11(o11), .in12(o12), .in13(o13), .in14(o14), .in15(o15), .in16(o16), .in17(o17),
    .in18(o18), .in19(o19), .in20(o20), .in21(o21), .in22(o22), .in23(o23), .in24(o24), .in25(o25),
    .in26(o26), .in27(o27), .in28(o28), .in29(o29), .in30(o30), .in31(o31), .out(RD2), .sel(A2));
endmodule

module TEST (
  input  [31:0] in_1,
  input  in_2,
  output [31:0] out_3
);

  wire clock_1_out;

  Register #(.width(32)) register_1 (.D(in_1), .en(in_2), .Q(out_3), .clk(clock_1_out));  // open: clr
  Clock clock_1 (.out(clock_1_out));
endmodule

module ALU (
  input  [2:0] ALUControl,
  input  [31:0] SrcA,
  input  [31:0] SrcB,
  output [31:0] ALUResult,
  output Zero
);

  wire comparator_1_lt, comparator_2_eq, comparator_3_eq;
  wire [31:0] add, \and , \or , slt, sub;

  Adder #(.width(32)) adder_1 (.a(SrcA), .b(SrcB), .out(add));  // open: cin, cout
  Subtractor #(.width(32)) subtractor_1 (.a(SrcA), .b(SrcB), .out(sub));  // open: bin, bout
  Comparator #(.width(32)) comparator_1 (.a(SrcA), .b(SrcB), .lt(comparator_1_lt));  // open: gt, eq
  assign \and  = SrcA & SrcB;  // AND_Gate and_1, 32 bits wide
  assign \or  = SrcA | SrcB;  // OR_Gate or_1, 32 bits wide
  assign slt = {{31{1'b0}}, comparator_1_lt};  // Bit_Extender bit_extender_1
  Multiplexer #(.select(3), .width(32), .enable("false")) multiplexer_1 (
    .in0(\and ), .in1(\or ), .in2(add), .in6(sub), .in7(slt), .out(ALUResult), .sel(ALUControl));  // open: in3, in4, in5
  Comparator #(.width(32)) comparator_2 (.a(sub), .b({32{1'b0}}), .eq(comparator_2_eq));  // open: gt, lt
  Comparator #(.width(3)) comparator_3 (.a(ALUControl), .b(3'b110), .eq(comparator_3_eq));  // open: gt, lt
  and and_2 (Zero, comparator_2_eq, comparator_3_eq);

  // Notes on the sheet:
  //   000
  //   001
  //   010
  //   110
  //   111
endmodule

module SPT (
  input  [31:0] in,
  output [15:0] _0_15,
  output [4:0] _16_20,
  output [4:0] _21_25,
  output [4:0] _11_15
);


  assign _0_15 = in[15:0];
  assign _11_15 = in[15:11];
  assign _16_20 = in[20:16];
  assign _21_25 = in[25:21];
endmodule

module EXT (
  input  [15:0] _15_0,
  output [31:0] SignImm
);

  assign SignImm = {{16{_15_0[15]}}, _15_0};  // Bit_Extender bit_extender_1
endmodule

module NXTAD (
  input  Branch,
  input  [31:0] Instr,
  input  Jump,
  input  Zero,
  input  [31:0] PC,
  input  [31:0] SignImm,
  output [31:0] PC_prime
);

  wire and_1_out;
  wire [31:0] beq, multiplexer_1_out, PC_4, shifter_1_out;

  Adder #(.width(32)) adder_1 (.a(PC), .b(32'h4), .out(PC_4));  // open: cin, cout
  Shifter #(.width(32)) shifter_1 (.in(SignImm), .\dist (5'b00010), .out(shifter_1_out));
  Adder #(.width(32)) adder_2 (.a(shifter_1_out), .b(PC), .out(beq));  // open: cin, cout
  and and_1 (and_1_out, Branch, Zero);
  Multiplexer #(.width(32), .enable("false")) multiplexer_1 (
    .in0(PC_4), .in1(beq), .out(multiplexer_1_out), .sel(and_1_out));
  Multiplexer #(.width(32), .enable("false")) multiplexer_2 (
    .in0(multiplexer_1_out), .in1({PC_4[31:28], Instr[25:0], 2'b00}), .out(PC_prime), .sel(Jump));
endmodule

module CU (
  input  [31:0] in,
  output RegWrite,
  output MemWrite,
  output [2:0] ALUControl,
  output ALUSrc,
  output MemtoReg,
  output RegDst,
  output Branch,
  output Jump
);

  wire add, addi, \and , beq, comparator_1_eq, comparator_2_eq, comparator_3_eq, comparator_4_eq,
       comparator_5_eq, j, lw, \or , or_1_out, or_2_out, or_3_out, or_4_out, or_5_out, pull_resistor_1_node,
       \R型指令 , slt, sub, sw;

  Comparator #(.width(6)) comparator_1 (.a(in[5:0]), .b(6'b100000), .eq(comparator_1_eq));  // open: gt, lt
  Comparator #(.width(6)) comparator_2 (.a(in[5:0]), .b(6'b100010), .eq(comparator_2_eq));  // open: gt, lt
  Comparator #(.width(6)) comparator_3 (.a(in[5:0]), .b(6'b100100), .eq(comparator_3_eq));  // open: gt, lt
  Comparator #(.width(6)) comparator_4 (.a(in[5:0]), .b(6'b100101), .eq(comparator_4_eq));  // open: gt, lt
  Comparator #(.width(6)) comparator_5 (.a(in[5:0]), .b(6'b101010), .eq(comparator_5_eq));  // open: gt, lt
  Comparator #(.width(6)) comparator_6 (.a(in[31:26]), .b(6'b100011), .eq(lw));  // open: gt, lt
  Comparator #(.width(6)) comparator_7 (.a(in[31:26]), .b(6'b101011), .eq(sw));  // open: gt, lt
  Comparator #(.width(6)) comparator_8 (.a(in[31:26]), .b(6'b000100), .eq(beq));  // open: gt, lt
  Comparator #(.width(6)) comparator_9 (.a(in[31:26]), .b({6{1'b0}}), .eq(\R型指令 ));  // open: gt, lt
  Comparator #(.width(6)) comparator_10 (.a(in[31:26]), .b(6'b001000), .eq(addi));  // open: gt, lt
  Comparator #(.width(6)) comparator_11 (.a(in[31:26]), .b(6'b000010), .eq(j));  // open: gt, lt
  and and_1 (add, comparator_1_eq, \R型指令 );
  and and_2 (sub, comparator_2_eq, \R型指令 );
  and and_3 (\and , comparator_3_eq, \R型指令 );
  and and_4 (\or , comparator_4_eq, \R型指令 );
  and and_5 (slt, comparator_5_eq, \R型指令 );
  or or_1 (or_1_out, lw, sw);
  or or_2 (or_2_out, sub, beq);
  or or_3 (or_3_out, or_2_out, or_1_out);
  or or_4 (or_4_out, add, sub, \and , \or , slt);
  Pull_Resistor pull_resistor_1 (.node(pull_resistor_1_node));
  or or_5 (or_5_out, add, or_3_out);
  or or_6 (RegWrite, \R型指令 , pull_resistor_1_node, addi, lw);
  or or_7 (MemWrite, pull_resistor_1_node, sw);
  or or_8 (ALUControl[0], pull_resistor_1_node, slt, \or );
  or or_9 (ALUControl[1], slt, pull_resistor_1_node, or_5_out);
  or or_10 (ALUControl[2], slt, pull_resistor_1_node, or_2_out);
  or or_11 (ALUSrc, addi, pull_resistor_1_node, or_1_out);
  or or_12 (MemtoReg, pull_resistor_1_node, lw);
  or or_13 (RegDst, pull_resistor_1_node, or_4_out);
  or or_14 (Branch, pull_resistor_1_node, beq);
  or or_15 (Jump, pull_resistor_1_node, j);

  // Other names for the same wires on the sheet: Funct[5:0] = in[5:0]; Op[5:0] = in[31:26]

  // Notes on the sheet:
  //   lw
  //   sw
  //   beq
  //   addi
  //   j
  //   001
  //   010
  //   000
  //   010
  //   010
  //   110
  //   110
  //   111
endmodule
